# Fritzing sketch circuit (saved by Fritzing 0.9.3b)
breadboards: 1

parts:
  BATT1 = 4xAA Switchable Battery Pack w/Bare Wire
  Micro_bit1 = Microbit
  U1 = L9110 H-bridge module [part_number="L9110 H-bridge"]
  LD1117AV33 = Voltage Regulator - 3.3V [part_number=LD1117AV33 package="TO220 [THT]"]
  M1 = DC Motor
  M2 = DC Motor

nets:
  N1: BATT1.POS, U1.VCC, LD1117AV33.Input_voltage
  GND: BATT1.NEG, Micro_bit1.GND, U1.GND, LD1117AV33.ADJ/GND
  N2: Micro_bit1.3V, LD1117AV33.Output
  N3: Micro_bit1.0, U1.A-IA
  N4: Micro_bit1.1, U1.A-IB
  N5: Micro_bit1.2, U1.B-IA
  N6: Micro_bit1.8, U1.B-IB
  N7: U1.MOTOR_A-A, M2.pin_1
  N8: U1.MOTOR_A-B, M2.pin_2
  N9: U1.MOTOR_B-A, M1.pin_2
  N10: U1.MOTOR_B-B, M1.pin_1

custom parts:
  4xAA Switchable Battery Pack w/Bare Wire: 4xAA Switchable Battery Pack with Bare Wire connection
  Microbit: BBC Microbit Fritzing part
  Voltage Regulator - 3.3V: 3.3V DC Voltage Regulator
